// Logisim project PLM.circ as structural Verilog: 4 circuits, main circuit main
module main (
  input  in_1,
  input  in_2,
  input  in_3,
  input  in_4,
  input  in_5,
  input  in_6,
  input  in_7,
  input  in_8,
  input  in_9,
  input  in_10,
  input  in_11,
  input  in_12,
  input  in_13,
  input  in_14,
  input  in_15,
  input  in_16
);

  wire and_1_out, and_2_out, and_3_out, button_1_out, clock_1_out, counter_1_carry, nflua4m4x4_1_out_27,
       nflua4m4x4_1_out_28, nflua4m4x4_1_out_29, nflua4m4x4_1_out_30, nflua4m4x4_1_out_31,
       nflua4m4x4_1_out_32, nflua4m4x4_1_out_33, nflua4m4x4_1_out_34, nflua4m4x4_1_out_35,
       nflua4m4x4_1_out_36, nflua4m4x4_1_out_37, nflua4m4x4_1_out_38, nflua4m4x4_1_out_39,
       nflua4m4x4_1_out_40, nflua4m4x4_1_out_41, nflua4m4x4_1_out_42, not_1_out, not_2_out, not_3_out,
       not_4_out, not_5_out, or_1_out, s_r_ff_1_q, s_r_ff_1_qn, s_r_ff_2_q, s_r_ff_2_qn;
  wire [9:0] counter_1_q;
  wire [15:0] rom_1_data;

  Button button_1 (.out(button_1_out));
  Clock clock_1 (.out(clock_1_out));
  S_R_Flip_Flop s_r_ff_1 (
    .S(counter_1_carry), .R(button_1_out), .clk(clock_1_out), .Q(s_r_ff_1_q), .Qn(s_r_ff_1_qn));  // open: reset, preset
  not not_1 (not_1_out, button_1_out);
  and and_1 (and_1_out, s_r_ff_1_qn, not_1_out);
  not not_2 (not_2_out, s_r_ff_1_q);
  and and_2 (and_2_out, not_2_out, clock_1_out);
  S_R_Flip_Flop s_r_ff_2 (
    .S(counter_1_carry), .R(or_1_out), .clk(not_3_out), .Q(s_r_ff_2_q), .Qn(s_r_ff_2_qn));  // open: reset, preset
  or or_1 (or_1_out, and_1_out, and_2_out);
  not not_3 (not_3_out, and_2_out);
  LED led_1 (.in(s_r_ff_2_q));
  and and_3 (and_3_out, s_r_ff_2_qn, and_2_out);
  not not_4 (not_4_out, and_3_out);
  Counter #(.max('h3ff), .width(10)) counter_1 (
    .Q(counter_1_q), .carry(counter_1_carry), .up(not_4_out), .clk(and_3_out));  // open: load, D, count, clr
  not not_5 (not_5_out, and_3_out);
  ROM #(.addrWidth(10), .dataWidth(16)) rom_1 (.addr(counter_1_q), .data(rom_1_data));
  LED led_2 (.in(nflua4m4x4_1_out_30));
  LED led_3 (.in(nflua4m4x4_1_out_29));
  LED led_4 (.in(nflua4m4x4_1_out_28));
  LED led_5 (.in(nflua4m4x4_1_out_27));
  LED led_6 (.in(nflua4m4x4_1_out_34));
  LED led_7 (.in(nflua4m4x4_1_out_33));
  LED led_8 (.in(nflua4m4x4_1_out_32));
  LED led_9 (.in(nflua4m4x4_1_out_31));
  LED led_10 (.in(nflua4m4x4_1_out_38));
  LED led_11 (.in(nflua4m4x4_1_out_37));
  LED led_12 (.in(nflua4m4x4_1_out_36));
  LED led_13 (.in(nflua4m4x4_1_out_35));
  LED led_14 (.in(nflua4m4x4_1_out_42));
  LED led_15 (.in(nflua4m4x4_1_out_41));
  LED led_16 (.in(nflua4m4x4_1_out_40));
  LED led_17 (.in(nflua4m4x4_1_out_39));
  NFLUA4M4X4 nflua4m4x4_1 (
    .in_18(rom_1_data[4]), .in_21(rom_1_data[8]), .in_24(rom_1_data[11]), .in_19(rom_1_data[5]),
    .in_22(rom_1_data[9]), .in_25(rom_1_data[13:12]), .in_20(rom_1_data[7:6]), .in_23(rom_1_data[10]),
    .in_26(not_5_out), .in_8(in_6), .in_10(in_12), .in_12(in_10), .in_14(in_16), .in_16(in_14), .in_2(in_4),
    .in_4(in_2), .in_6(in_8), .in_7(in_7), .in_9(in_5), .in_11(in_11), .in_13(in_9), .in_15(in_15),
    .in_17(in_13), .in_1(rom_1_data[3:0]), .in_3(in_3), .in_5(in_1), .out_33(nflua4m4x4_1_out_33),
    .out_35(nflua4m4x4_1_out_35), .out_37(nflua4m4x4_1_out_37), .out_39(nflua4m4x4_1_out_39),
    .out_41(nflua4m4x4_1_out_41), .out_27(nflua4m4x4_1_out_27), .out_29(nflua4m4x4_1_out_29),
    .out_31(nflua4m4x4_1_out_31), .out_34(nflua4m4x4_1_out_34), .out_36(nflua4m4x4_1_out_36),
    .out_38(nflua4m4x4_1_out_38), .out_40(nflua4m4x4_1_out_40), .out_42(nflua4m4x4_1_out_42),
    .out_28(nflua4m4x4_1_out_28), .out_30(nflua4m4x4_1_out_30), .out_32(nflua4m4x4_1_out_32));
  // also tied to GND on the sheet: {rom_1_data[14], rom_1_data[15]}

  // Notes on the sheet:
  //   Recon
  //   Finish
  //   contents of rom_1 (hex, n*v repeats v):
  //   10 14 18 1c 11 15 19 1d 12 16 1a 1e 13 17 1b 1f 60 a00 1a00 3600 200 1300 2a00 24 a04 2604
endmodule

module NFLUA2M4 (
  input  CLK,
  input  [1:0] ALU,
  input  [1:0] SEL,
  input  [1:0] IOSEL,
  input  MIN,
  input  MOUT,
  input  PERF,
  input  ABIO,
  input  [1:0] SELT,
  input  SETT,
  input  RST,
  input  A,
  input  B,
  input  C,
  input  D,
  output out_16,
  output out_17,
  output out_18,
  output out_19,
  output out_20,
  output out_21,
  output out_22,
  output out_23
);

  wire and_1_out, and_2_out, and_3_out, and_4_out, and_5_out, and_6_out, and_7_out, and_8_out, and_9_out,
       and_10_out, and_11_out, and_12_out, and_13_out, and_14_out, and_15_out, and_16_out, and_17_out,
       and_18_out, and_19_out, and_20_out, and_21_out, and_22_out, and_23_out, and_24_out, and_25_out,
       and_26_out, and_27_out, and_28_out, and_29_out, and_34_out, and_35_out, and_36_out, and_37_out,
       and_38_out, and_39_out, and_40_out, and_41_out, and_42_out, and_43_out, and_44_out, and_45_out,
       and_46_out, and_47_out, and_48_out, and_49_out, and_50_out, and_51_out, and_52_out, and_53_out,
       and_54_out, and_55_out, and_56_out, comparator_1_eq, comparator_2_eq, comparator_3_eq,
       comparator_4_eq, comparator_5_eq, comparator_6_eq, comparator_7_eq, comparator_8_eq, comparator_9_eq,
       not_1_out, not_2_out, not_3_out, not_4_out, not_5_out, or_1_out, or_2_out, or_3_out, or_4_out,
       or_5_out, or_6_out, or_7_out, or_8_out, or_9_out, or_10_out, or_11_out, or_12_out, s_r_ff_1_q,
       s_r_ff_2_q, s_r_ff_3_q, s_r_ff_4_q, s_r_ff_5_q, s_r_ff_6_q, s_r_ff_7_q, s_r_ff_8_q, s_r_ff_9_q,
       s_r_ff_9_qn, s_r_ff_10_q, s_r_ff_10_qn, s_r_ff_11_q, s_r_ff_11_qn, s_r_ff_12_q, s_r_ff_12_qn;

  Comparator #(.width(2)) comparator_1 (.a(ALU), .b(SEL), .eq(comparator_1_eq));  // open: gt, lt
  and and_1 (and_1_out, MIN, PERF);
  and and_2 (and_2_out, MOUT, PERF);
  and and_3 (and_3_out, MIN, PERF);
  and and_4 (and_4_out, MOUT, PERF);
  and and_5 (and_5_out, MIN, PERF);
  and and_6 (and_6_out, MOUT, PERF);
  and and_7 (and_7_out, MIN, PERF);
  and and_8 (and_8_out, MOUT, PERF);
  and and_9 (and_9_out, comparator_1_eq, SETT);
  Comparator #(.width(2)) comparator_2 (.a(IOSEL), .b(2'b00), .eq(comparator_2_eq));  // open: gt, lt
  Comparator #(.width(2)) comparator_3 (.a(IOSEL), .b(2'b01), .eq(comparator_3_eq));  // open: gt, lt
  Comparator #(.width(2)) comparator_4 (.a(IOSEL), .b(2'b10), .eq(comparator_4_eq));  // open: gt, lt
  Comparator #(.width(2)) comparator_5 (.a(IOSEL), .b(2'b11), .eq(comparator_5_eq));  // open: gt, lt
  Comparator #(.width(2)) comparator_6 (.a(SELT), .b(2'b00), .eq(comparator_6_eq));  // open: gt, lt
  Comparator #(.width(2)) comparator_7 (.a(SELT), .b(2'b01), .eq(comparator_7_eq));  // open: gt, lt
  Comparator #(.width(2)) comparator_8 (.a(SELT), .b(2'b10), .eq(comparator_8_eq));  // open: gt, lt
  Comparator #(.width(2)) comparator_9 (.a(SELT), .b(2'b11), .eq(comparator_9_eq));  // open: gt, lt
  and and_10 (and_10_out, ABIO, PERF, comparator_2_eq);
  and and_11 (and_11_out, PERF, ABIO, comparator_3_eq);
  and and_12 (and_12_out, ABIO, PERF, comparator_4_eq);
  and and_13 (and_13_out, PERF, ABIO, comparator_5_eq);
  and and_14 (and_14_out, and_1_out, comparator_2_eq);
  and and_15 (and_15_out, comparator_2_eq, and_2_out);
  and and_16 (and_16_out, and_3_out, comparator_3_eq);
  and and_17 (and_17_out, comparator_3_eq, and_4_out);
  and and_18 (and_18_out, and_5_out, comparator_4_eq);
  and and_19 (and_19_out, comparator_4_eq, and_6_out);
  and and_20 (and_20_out, and_7_out, comparator_5_eq);
  and and_21 (and_21_out, comparator_5_eq, and_8_out);
  and and_22 (and_22_out, and_9_out, comparator_6_eq);
  and and_23 (and_23_out, and_9_out, RST);
  and and_24 (and_24_out, and_9_out, comparator_7_eq);
  and and_25 (and_25_out, and_9_out, RST);
  and and_26 (and_26_out, and_9_out, comparator_8_eq);
  and and_27 (and_27_out, and_9_out, RST);
  and and_28 (and_28_out, and_9_out, comparator_9_eq);
  and and_29 (and_29_out, and_9_out, RST);
  and and_30 (out_17, or_10_out, out_16);
  S_R_Flip_Flop s_r_ff_1 (
    .S(and_14_out), .R(and_15_out), .clk(and_34_out), .Q(s_r_ff_1_q), .Qn(out_16));  // open: reset, preset
  and and_31 (out_19, or_10_out, out_18);
  S_R_Flip_Flop s_r_ff_2 (
    .S(and_16_out), .R(and_17_out), .clk(and_34_out), .Q(s_r_ff_2_q), .Qn(out_18));  // open: reset, preset
  and and_32 (out_21, or_10_out, out_20);
  S_R_Flip_Flop s_r_ff_3 (
    .S(and_18_out), .R(and_19_out), .clk(and_34_out), .Q(s_r_ff_3_q), .Qn(out_20));  // open: reset, preset
  and and_33 (out_23, or_10_out, out_22);
  S_R_Flip_Flop s_r_ff_4 (
    .S(and_20_out), .R(and_21_out), .clk(and_34_out), .Q(s_r_ff_4_q), .Qn(out_22));  // open: reset, preset
  S_R_Flip_Flop s_r_ff_5 (.S(and_22_out), .R(and_23_out), .clk(CLK), .Q(s_r_ff_5_q));  // open: reset, Qn, preset
  S_R_Flip_Flop s_r_ff_6 (.S(and_24_out), .R(and_25_out), .clk(CLK), .Q(s_r_ff_6_q));  // open: reset, Qn, preset
  S_R_Flip_Flop s_r_ff_7 (.S(and_26_out), .R(and_27_out), .clk(CLK), .Q(s_r_ff_7_q));  // open: reset, Qn, preset
  S_R_Flip_Flop s_r_ff_8 (.S(and_28_out), .R(and_29_out), .clk(CLK), .Q(s_r_ff_8_q));  // open: reset, Qn, preset
  and and_34 (and_34_out, CLK, comparator_1_eq);
  and and_35 (and_35_out, A, s_r_ff_1_q);
  and and_36 (and_36_out, B, s_r_ff_2_q);
  and and_37 (and_37_out, C, s_r_ff_3_q);
  and and_38 (and_38_out, D, s_r_ff_4_q);
  S_R_Flip_Flop s_r_ff_9 (
    .S(and_10_out), .R(not_1_out), .clk(and_39_out), .Q(s_r_ff_9_q), .Qn(s_r_ff_9_qn));  // open: reset, preset
  not not_1 (not_1_out, and_10_out);
  and and_39 (and_39_out, comparator_2_eq, and_34_out, PERF);
  S_R_Flip_Flop s_r_ff_10 (
    .S(and_11_out), .R(not_2_out), .clk(and_40_out), .Q(s_r_ff_10_q), .Qn(s_r_ff_10_qn));  // open: reset, preset
  not not_2 (not_2_out, and_11_out);
  and and_40 (and_40_out, comparator_3_eq, and_34_out, PERF);
  S_R_Flip_Flop s_r_ff_11 (
    .S(and_12_out), .R(not_3_out), .clk(and_41_out), .Q(s_r_ff_11_q), .Qn(s_r_ff_11_qn));  // open: reset, preset
  not not_3 (not_3_out, and_12_out);
  and and_41 (and_41_out, comparator_4_eq, and_34_out, PERF);
  S_R_Flip_Flop s_r_ff_12 (
    .S(and_13_out), .R(not_4_out), .clk(and_42_out), .Q(s_r_ff_12_q), .Qn(s_r_ff_12_qn));  // open: reset, preset
  not not_4 (not_4_out, and_13_out);
  and and_42 (and_42_out, comparator_5_eq, and_34_out, PERF);
  and and_43 (and_43_out, and_35_out, s_r_ff_9_q);
  or or_1 (or_1_out, and_44_out, or_5_out);
  and and_44 (and_44_out, and_35_out, s_r_ff_9_qn);
  and and_45 (and_45_out, and_36_out, s_r_ff_10_q);
  and and_46 (and_46_out, and_36_out, s_r_ff_10_qn);
  and and_47 (and_47_out, and_37_out, s_r_ff_11_q);
  or or_2 (or_2_out, and_48_out, and_50_out);
  and and_48 (and_48_out, and_37_out, s_r_ff_11_qn);
  and and_49 (and_49_out, and_38_out, s_r_ff_12_q);
  and and_50 (and_50_out, and_38_out, s_r_ff_12_qn);
  or or_3 (or_3_out, and_43_out, or_4_out);
  or or_4 (or_4_out, or_6_out, and_45_out);
  or or_5 (or_5_out, and_46_out, or_2_out);
  or or_6 (or_6_out, and_47_out, and_49_out);
  and and_51 (and_51_out, or_1_out, or_3_out);
  or or_7 (or_7_out, or_1_out, or_3_out);
  or or_8 (or_8_out, or_1_out, or_3_out);
  and and_52 (and_52_out, or_7_out, s_r_ff_7_q);
  not not_5 (not_5_out, or_8_out);
  and and_53 (and_53_out, and_51_out, s_r_ff_6_q);
  and and_54 (and_54_out, not_5_out, s_r_ff_8_q);
  and and_55 (and_55_out, or_1_out, s_r_ff_5_q);
  and and_56 (and_56_out, or_3_out, s_r_ff_5_q);
  or or_9 (or_9_out, and_55_out, and_56_out);
  or or_10 (or_10_out, or_9_out, or_11_out);
  or or_11 (or_11_out, and_53_out, or_12_out);
  or or_12 (or_12_out, and_52_out, and_54_out);

  // Notes on the sheet:
  //   EN
  //   PSTH
  //   AND
  //   OR
  //   NOT
endmodule

module CMPPSTH2 (
  input  [1:0] in_1,
  input  [1:0] in_2,
  input  [1:0] in_3,
  output [1:0] out_4
);

  wire comparator_1_eq;

  Comparator #(.width(2)) comparator_1 (.a(in_1), .b(in_2), .eq(comparator_1_eq));  // open: gt, lt
  and and_1 (out_4[0], in_3[0], comparator_1_eq);
  and and_2 (out_4[1], comparator_1_eq, in_3[1]);
endmodule

module NFLUA4M4X4 (
  input  [3:0] in_1,
  input  in_2,
  input  in_3,
  input  in_4,
  input  in_5,
  input  in_6,
  input  in_7,
  input  in_8,
  input  in_9,
  input  in_10,
  input  in_11,
  input  in_12,
  input  in_13,
  input  in_14,
  input  in_15,
  input  in_16,
  input  in_17,
  input  in_18,
  input  in_19,
  input  [1:0] in_20,
  input  in_21,
  input  in_22,
  input  in_23,
  input  in_24,
  input  [1:0] in_25,
  input  in_26,
  output out_27,
  output out_28,
  output out_29,
  output out_30,
  output out_31,
  output out_32,
  output out_33,
  output out_34,
  output out_35,
  output out_36,
  output out_37,
  output out_38,
  output out_39,
  output out_40,
  output out_41,
  output out_42
);

  wire nflua2m4_1_out_21, nflua2m4_1_out_23, nflua2m4_2_out_17, nflua2m4_2_out_21, nflua2m4_2_out_23,
       nflua2m4_3_out_17, nflua2m4_3_out_21, nflua2m4_3_out_23, nflua2m4_4_out_17, nflua2m4_4_out_21,
       nflua2m4_5_out_19, nflua2m4_5_out_21, nflua2m4_5_out_23, nflua2m4_6_out_17, nflua2m4_6_out_19,
       nflua2m4_6_out_21, nflua2m4_6_out_23, nflua2m4_7_out_17, nflua2m4_7_out_19, nflua2m4_7_out_21,
       nflua2m4_7_out_23, nflua2m4_8_out_17, nflua2m4_8_out_19, nflua2m4_8_out_21, nflua2m4_9_out_19,
       nflua2m4_9_out_21, nflua2m4_9_out_23, nflua2m4_10_out_17, nflua2m4_10_out_19, nflua2m4_10_out_21,
       nflua2m4_10_out_23, nflua2m4_11_out_17, nflua2m4_11_out_19, nflua2m4_11_out_21, nflua2m4_11_out_23,
       nflua2m4_12_out_17, nflua2m4_12_out_19, nflua2m4_12_out_21, nflua2m4_13_out_19, nflua2m4_13_out_23,
       nflua2m4_14_out_17, nflua2m4_14_out_19, nflua2m4_14_out_23, nflua2m4_15_out_17, nflua2m4_15_out_19,
       nflua2m4_15_out_23, nflua2m4_16_out_17, nflua2m4_16_out_19;
  wire [1:0] cmppsth2_1_out_4, cmppsth2_2_out_4, cmppsth2_3_out_4, cmppsth2_4_out_4;

  CMPPSTH2 cmppsth2_1 (.in_1(2'b00), .in_2(in_1[1:0]), .in_3(in_1[3:2]), .out_4(cmppsth2_1_out_4));
  NFLUA2M4 nflua2m4_1 (
    .CLK(in_26), .ALU(2'b00), .SEL(cmppsth2_1_out_4), .IOSEL(in_25), .MIN(in_24), .MOUT(in_23), .PERF(in_22),
    .ABIO(in_21), .SELT(in_20), .SETT(in_19), .RST(in_18), .C(nflua2m4_5_out_19), .D(nflua2m4_2_out_17),
    .A(in_17), .B(in_13), .out_21(nflua2m4_1_out_21), .out_23(nflua2m4_1_out_23), .out_17(out_42),
    .out_19(out_38));  // open: out_20, out_22, out_16, out_18
  NFLUA2M4 nflua2m4_2 (
    .CLK(in_26), .ALU(2'b01), .SEL(cmppsth2_1_out_4), .IOSEL(in_25), .MIN(in_24), .MOUT(in_23), .PERF(in_22),
    .ABIO(in_21), .SELT(in_20), .SETT(in_19), .RST(in_18), .C(nflua2m4_6_out_19), .D(nflua2m4_3_out_17),
    .A(nflua2m4_1_out_23), .B(in_12), .out_21(nflua2m4_2_out_21), .out_23(nflua2m4_2_out_23),
    .out_17(nflua2m4_2_out_17), .out_19(out_37));  // open: out_20, out_22, out_16, out_18
  NFLUA2M4 nflua2m4_3 (
    .CLK(in_26), .ALU(2'b10), .SEL(cmppsth2_1_out_4), .IOSEL(in_25), .MIN(in_24), .MOUT(in_23), .PERF(in_22),
    .ABIO(in_21), .SELT(in_20), .SETT(in_19), .RST(in_18), .C(nflua2m4_7_out_19), .D(nflua2m4_4_out_17),
    .A(nflua2m4_2_out_23), .B(in_11), .out_21(nflua2m4_3_out_21), .out_23(nflua2m4_3_out_23),
    .out_17(nflua2m4_3_out_17), .out_19(out_36));  // open: out_20, out_22, out_16, out_18
  NFLUA2M4 nflua2m4_4 (
    .CLK(in_26), .ALU(2'b11), .SEL(cmppsth2_1_out_4), .IOSEL(in_25), .MIN(in_24), .MOUT(in_23), .PERF(in_22),
    .ABIO(in_21), .SELT(in_20), .SETT(in_19), .RST(in_18), .C(nflua2m4_8_out_19), .D(in_5),
    .A(nflua2m4_3_out_23), .B(in_10), .out_21(nflua2m4_4_out_21), .out_23(out_30),
    .out_17(nflua2m4_4_out_17), .out_19(out_35));  // open: out_20, out_22, out_16, out_18
  CMPPSTH2 cmppsth2_2 (.in_1(2'b01), .in_2(in_1[1:0]), .in_3(in_1[3:2]), .out_4(cmppsth2_2_out_4));
  NFLUA2M4 nflua2m4_5 (
    .CLK(in_26), .ALU(2'b00), .SEL(cmppsth2_2_out_4), .IOSEL(in_25), .MIN(in_24), .MOUT(in_23), .PERF(in_22),
    .ABIO(in_21), .SELT(in_20), .SETT(in_19), .RST(in_18), .C(nflua2m4_9_out_19), .D(nflua2m4_6_out_17),
    .A(in_16), .B(nflua2m4_1_out_21), .out_21(nflua2m4_5_out_21), .out_23(nflua2m4_5_out_23),
    .out_17(out_41), .out_19(nflua2m4_5_out_19));  // open: out_20, out_22, out_16, out_18
  NFLUA2M4 nflua2m4_6 (
    .CLK(in_26), .ALU(2'b01), .SEL(cmppsth2_2_out_4), .IOSEL(in_25), .MIN(in_24), .MOUT(in_23), .PERF(in_22),
    .ABIO(in_21), .SELT(in_20), .SETT(in_19), .RST(in_18), .C(nflua2m4_10_out_19), .D(nflua2m4_7_out_17),
    .A(nflua2m4_5_out_23), .B(nflua2m4_2_out_21), .out_21(nflua2m4_6_out_21), .out_23(nflua2m4_6_out_23),
    .out_17(nflua2m4_6_out_17), .out_19(nflua2m4_6_out_19));  // open: out_20, out_22, out_16, out_18
  NFLUA2M4 nflua2m4_7 (
    .CLK(in_26), .ALU(2'b10), .SEL(cmppsth2_2_out_4), .IOSEL(in_25), .MIN(in_24), .MOUT(in_23), .PERF(in_22),
    .ABIO(in_21), .SELT(in_20), .SETT(in_19), .RST(in_18), .C(nflua2m4_11_out_19), .D(nflua2m4_8_out_17),
    .A(nflua2m4_6_out_23), .B(nflua2m4_3_out_21), .out_21(nflua2m4_7_out_21), .out_23(nflua2m4_7_out_23),
    .out_17(nflua2m4_7_out_17), .out_19(nflua2m4_7_out_19));  // open: out_20, out_22, out_16, out_18
  NFLUA2M4 nflua2m4_8 (
    .CLK(in_26), .ALU(2'b11), .SEL(cmppsth2_2_out_4), .IOSEL(in_25), .MIN(in_24), .MOUT(in_23), .PERF(in_22),
    .ABIO(in_21), .SELT(in_20), .SETT(in_19), .RST(in_18), .C(nflua2m4_12_out_19), .D(in_4),
    .A(nflua2m4_7_out_23), .B(nflua2m4_4_out_21), .out_21(nflua2m4_8_out_21), .out_23(out_29),
    .out_17(nflua2m4_8_out_17), .out_19(nflua2m4_8_out_19));  // open: out_20, out_22, out_16, out_18
  CMPPSTH2 cmppsth2_3 (.in_1(2'b10), .in_2(in_1[1:0]), .in_3(in_1[3:2]), .out_4(cmppsth2_3_out_4));
  NFLUA2M4 nflua2m4_9 (
    .CLK(in_26), .ALU(2'b00), .SEL(cmppsth2_3_out_4), .IOSEL(in_25), .MIN(in_24), .MOUT(in_23), .PERF(in_22),
    .ABIO(in_21), .SELT(in_20), .SETT(in_19), .RST(in_18), .C(nflua2m4_13_out_19), .D(nflua2m4_10_out_17),
    .A(in_15), .B(nflua2m4_5_out_21), .out_21(nflua2m4_9_out_21), .out_23(nflua2m4_9_out_23),
    .out_17(out_40), .out_19(nflua2m4_9_out_19));  // open: out_20, out_22, out_16, out_18
  NFLUA2M4 nflua2m4_10 (
    .CLK(in_26), .ALU(2'b01), .SEL(cmppsth2_3_out_4), .IOSEL(in_25), .MIN(in_24), .MOUT(in_23), .PERF(in_22),
    .ABIO(in_21), .SELT(in_20), .SETT(in_19), .RST(in_18), .C(nflua2m4_14_out_19), .D(nflua2m4_11_out_17),
    .A(nflua2m4_9_out_23), .B(nflua2m4_6_out_21), .out_21(nflua2m4_10_out_21), .out_23(nflua2m4_10_out_23),
    .out_17(nflua2m4_10_out_17), .out_19(nflua2m4_10_out_19));  // open: out_20, out_22, out_16, out_18
  NFLUA2M4 nflua2m4_11 (
    .CLK(in_26), .ALU(2'b10), .SEL(cmppsth2_3_out_4), .IOSEL(in_25), .MIN(in_24), .MOUT(in_23), .PERF(in_22),
    .ABIO(in_21), .SELT(in_20), .SETT(in_19), .RST(in_18), .C(nflua2m4_15_out_19), .D(nflua2m4_12_out_17),
    .A(nflua2m4_10_out_23), .B(nflua2m4_7_out_21), .out_21(nflua2m4_11_out_21), .out_23(nflua2m4_11_out_23),
    .out_17(nflua2m4_11_out_17), .out_19(nflua2m4_11_out_19));  // open: out_20, out_22, out_16, out_18
  NFLUA2M4 nflua2m4_12 (
    .CLK(in_26), .ALU(2'b11), .SEL(cmppsth2_3_out_4), .IOSEL(in_25), .MIN(in_24), .MOUT(in_23), .PERF(in_22),
    .ABIO(in_21), .SELT(in_20), .SETT(in_19), .RST(in_18), .C(nflua2m4_16_out_19), .D(in_3),
    .A(nflua2m4_11_out_23), .B(nflua2m4_8_out_21), .out_21(nflua2m4_12_out_21), .out_23(out_28),
    .out_17(nflua2m4_12_out_17), .out_19(nflua2m4_12_out_19));  // open: out_20, out_22, out_16, out_18
  CMPPSTH2 cmppsth2_4 (.in_1(2'b11), .in_2(in_1[1:0]), .in_3(in_1[3:2]), .out_4(cmppsth2_4_out_4));
  NFLUA2M4 nflua2m4_13 (
    .CLK(in_26), .ALU(2'b00), .SEL(cmppsth2_4_out_4), .IOSEL(in_25), .MIN(in_24), .MOUT(in_23), .PERF(in_22),
    .ABIO(in_21), .SELT(in_20), .SETT(in_19), .RST(in_18), .C(in_9), .D(nflua2m4_14_out_17), .A(in_14),
    .B(nflua2m4_9_out_21), .out_21(out_34), .out_23(nflua2m4_13_out_23), .out_17(out_39),
    .out_19(nflua2m4_13_out_19));  // open: out_20, out_22, out_16, out_18
  NFLUA2M4 nflua2m4_14 (
    .CLK(in_26), .ALU(2'b01), .SEL(cmppsth2_4_out_4), .IOSEL(in_25), .MIN(in_24), .MOUT(in_23), .PERF(in_22),
    .ABIO(in_21), .SELT(in_20), .SETT(in_19), .RST(in_18), .C(in_8), .D(nflua2m4_15_out_17),
    .A(nflua2m4_13_out_23), .B(nflua2m4_10_out_21), .out_21(out_33), .out_23(nflua2m4_14_out_23),
    .out_17(nflua2m4_14_out_17), .out_19(nflua2m4_14_out_19));  // open: out_20, out_22, out_16, out_18
  NFLUA2M4 nflua2m4_15 (
    .CLK(in_26), .ALU(2'b10), .SEL(cmppsth2_4_out_4), .IOSEL(in_25), .MIN(in_24), .MOUT(in_23), .PERF(in_22),
    .ABIO(in_21), .SELT(in_20), .SETT(in_19), .RST(in_18), .C(in_7), .D(nflua2m4_16_out_17),
    .A(nflua2m4_14_out_23), .B(nflua2m4_11_out_21), .out_21(out_32), .out_23(nflua2m4_15_out_23),
    .out_17(nflua2m4_15_out_17), .out_19(nflua2m4_15_out_19));  // open: out_20, out_22, out_16, out_18
  NFLUA2M4 nflua2m4_16 (
    .CLK(in_26), .ALU(2'b11), .SEL(cmppsth2_4_out_4), .IOSEL(in_25), .MIN(in_24), .MOUT(in_23), .PERF(in_22),
    .ABIO(in_21), .SELT(in_20), .SETT(in_19), .RST(in_18), .C(in_6), .D(in_2), .A(nflua2m4_15_out_23),
    .B(nflua2m4_12_out_21), .out_21(out_31), .out_23(out_27), .out_17(nflua2m4_16_out_17),
    .out_19(nflua2m4_16_out_19));  // open: out_20, out_22, out_16, out_18
endmodule
